# Fritzing sketch Schema (saved by Fritzing 0.9.3b)
breadboards: 1

parts:
  Mod1 = Raspberry Pi Pico W
  DHT11_1 = DHT11 module
  LED1 = LED - 5mm [color="Red (633nm)" package="5 mm [THT]"]
  LED2 = LED - 5mm [color="Green (565nm)" package="5 mm [THT]"]
  R1 = Resistor [tolerance=±5% resistance=330 package="0603 [SMD]"]
  R2 = Resistor [tolerance=±5% resistance=330 package="0603 [SMD]"]
  Mod2 = KY-022 Infrared Receiver Module [package="Breakout board"]
  LED4 = LED - 5mm [color="Yellow (595nm)" package="5 mm [THT]"]
  R3 = Resistor [tolerance=±5% resistance=330 package="0603 [SMD]"]

nets:
  N1: Mod1.pin_3, Mod1.pin_8, Mod1.pin_13, Mod1.pin_18, Mod1.pin_23, Mod1.pin_28, Mod1.pin_33, Mod1.pin_38, DHT11_1.GND, R1.Pin_1, R2.Pin_1, Mod2.-, R3.Pin_1
  N2: Mod1.pin_17, LED4.anode
  N3: Mod1.pin_19, LED1.anode
  N4: Mod1.pin_20, LED2.anode
  N5: Mod1.pin_21, DHT11_1.VCC
  N6: Mod1.pin_25, Mod2.S
  N7: Mod1.pin_36, DHT11_1.DATA, Mod2.Vin
  N8: LED1.cathode, R1.Pin_0
  N9: LED2.cathode, R2.Pin_0
  N10: LED4.cathode, R3.Pin_0

custom parts:
  Raspberry Pi Pico W: Raspberry Pi Pico W. Based around the RP2040 microcontroller the Pico W is a low cost microcontroller device bringing Raspberry Pi quality, cost, and easy of use to the microcontroller space. The areas marked KEEPOUT in pcb silkscreen should not have traces running through them to avoid shorts on a soldered in module!
  DHT11 module: https://cdn-learn.adafruit.com/downloads/pdf/dht.pdf DHT11 black pcb module reference by:https://github.com/adafruit/Fritzing-Library/blob/master/parts/DHT11%20Humitidy%20and%20Temperature%20Sensor.fzpz
  KY-022 Infrared Receiver Module: KY-022 IR receiver module, reacts to 38kHz infrared light.
